# Fritzing sketch Sketch (saved by Fritzing 1.0.4)
circuit board: 11.5476cm x 7.32837cm
breadboards: 1

parts:
  S1 = Pushbutton [package="[THT]"]
  S2 = Toggle Switch [package=THT]
  R1 = Resistor [tolerance=±5% power=0.25W resistance=1M package=THT]
  R2 = Resistor [tolerance=±5% power=0.25W resistance=1M package=THT]
  C1 = Electrolytic Capacitor [capacitance=0.1µF voltage=50V package="1010 [SMD, electrolytic]"]
  R3 = Rotary Potentiometer (Large) [maximum_resistance=10kΩ knob_status=50% power=0.5W package=THT]
  ZS-042_RTC1 = ZS-042 RTC Module
  U1 = LIPO-2000mAh [package=lipo-2000]
  Part1 = Adafruit SDIO microSD Breakout
  A2 = Waveshare e-Paper HAT with 7in display [package=THT]
  C3 = Electrolytic Capacitor [capacitance=0.1µF voltage=50V package="1010 [SMD, electrolytic]"]
  A4 = Arduino Nano ESP32

nets:
  GND: S1.Pin_1, S1.Pin_2, S2.L1, R2.Pin_1, C1.-, R3.leg1, ZS-042_RTC1.GND, U1.-, Part1.GND, A2.pin_7, C3.-, A4.Pin_14, A4.Pin_19
  N1: S1.Pin_3, S1.Pin_4, A4.Pin_18
  N2: S2.COM, R1.Pin_0, A4.Pin_15
  N3: S2.L2, U1.+
  N4: R1.Pin_1, R2.Pin_0, C1.+, A4.Pin_11
  N5: R3.wiper, C3.+, A4.Pin_9
  N6: R3.leg2, A4.Pin_8
  N7: ZS-042_RTC1.SDA, A4.Pin_6
  N8: ZS-042_RTC1.SCL, A4.Pin_7
  N9: Part1.3.3V, A2.pin_8, A4.Pin_2
  N10: Part1.SCLK, A4.Pin_24
  N11: Part1.DO, A4.Pin_23
  N12: Part1.DI, A4.Pin_22
  N13: Part1.CS, A4.Pin_21
  N14: A2.pin_1, A4.Pin_30
  N15: A2.pin_2, A4.Pin_29
  N16: A2.pin_3, A4.Pin_28
  N17: A2.pin_4, A4.Pin_27
  N18: A2.pin_5, A4.Pin_26
  N19: A2.pin_6, A4.Pin_25

custom parts:
  Waveshare e-Paper HAT with 7in display: .This is a universal driver board for e-Paper raw panels, can be used to drive various SPI interface e-Paper from Waveshare. This version includes a 7in display panel in breadboard.
  Arduino Nano ESP32: Arduino® Nano ESP32 tht.
